# Fritzing sketch hub (saved by Fritzing 0.9.2b)
breadboards: 1

parts:
  nRF24L01 = nRF24L01
  C3 = Electrolytic Capacitor [capacitance=1µF package="100 mil [THT, electrolytic]"]
  MCU = Arduino Nano (Rev3.0)
  R7 = Resistor [tolerance=±5% resistance=100 package=THT]
  R8 = Resistor [tolerance=±5% resistance=220 package=THT]
  R9 = Resistor [tolerance=±5% resistance=220 package=THT]
  LED1 = LED - 5mm [color="Blue (470nm)" package="5 mm [THT]"]

nets:
  N1: nRF24L01.VCC, C3.+, R7.Pin_1, R8.Pin_0
  N2: nRF24L01.CSN, MCU.D10
  N3: nRF24L01.MOSI, MCU.D11/MOSI
  GND: nRF24L01.GND, C3.-, MCU.GND, R8.Pin_1, R9.Pin_1
  N4: nRF24L01.CE, MCU.D9
  N5: nRF24L01.SCK, MCU.D13/SCK
  N6: nRF24L01.MISO, MCU.D12/MISO
  N7: MCU.D3, LED1.anode
  N8: MCU.5V, R7.Pin_0
  N9: R9.Pin_0, LED1.cathode

custom parts:
  nRF24L01: nRF24L01 module
