# Fritzing sketch hub (saved by Fritzing 0.9.2b)
breadboards: 1

parts:
  U1 = Spark Core (v1.0)
  nRF24L01P = nRF24L01
  C2 = Electrolytic Capacitor [capacitance=1µF package="100 mil [THT, electrolytic]"]

nets:
  3V3: U1.A2, U1.3V3, nRF24L01P.VCC, nRF24L01P.CSN, C2.+
  N1: U1.A3, U1.A6, nRF24L01P.SCK
  N2: U1.A4, nRF24L01P.MISO
  N3: U1.A5, U1.VIN, nRF24L01P.MOSI
  GND: U1.GND, nRF24L01P.GND, C2.-
  N4: U1.D6, nRF24L01P.CE

custom parts:
  Spark Core (v1.0): The Spark Core is a tiny Wi-Fi development board that makes it easy to create internet-connected hardware. The Core is all you need to get started; power it over USB and in minutes you'll be controlling LEDs, switches and motors and collecting data from sensors over the internet! It has 8 digital I/O pins, 8 analog I/O pins, 8 PWM pins; UART (Serial), SPI, I2C, and JTAG peripherals available.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
  nRF24L01: nRF24L01 module
