# Fritzing sketch hub (saved by Fritzing 0.9.2b)

parts:
  nRF24L1 = nRF24L01
  C1 = Electrolytic Capacitor [capacitance=1µF package="100 mil [THT, electrolytic]"]
  Raspberry_Pi2 = Raspberry Pi B rev2

nets:
  VCC: nRF24L1.VCC, C1.+, Raspberry_Pi2.3V3
  N1: nRF24L1.CSN, Raspberry_Pi2.GPIO_8
  N2: nRF24L1.MOSI, Raspberry_Pi2.GPIO_10
  GND: nRF24L1.GND, C1.-, Raspberry_Pi2.GND
  N3: nRF24L1.CE, Raspberry_Pi2.GPIO_25
  N4: nRF24L1.SCK, Raspberry_Pi2.GPIO_11
  N5: nRF24L1.MISO, Raspberry_Pi2.GPIO_9

custom parts:
  nRF24L01: nRF24L01 module
