# Fritzing sketch nano (saved by Fritzing 0.9.2b)
breadboards: 1

parts:
  nRF24L01 = nRF24L01
  C3 = Electrolytic Capacitor [capacitance=1µF package="100 mil [THT, electrolytic]"]
  MCU = Arduino Nano (Rev3.0)
  S1 = Pushbutton [package="[THT]"]

nets:
  VCC: nRF24L01.VCC, C3.+, MCU.3V3
  N1: nRF24L01.CSN, MCU.D10
  N2: nRF24L01.MOSI, MCU.D11/MOSI
  GND: nRF24L01.GND, C3.-, MCU.GND, S1.Pin_1, S1.Pin_2
  N3: nRF24L01.CE, MCU.D9
  N4: nRF24L01.SCK, MCU.D13/SCK
  N5: nRF24L01.MISO, MCU.D12/MISO
  N6: MCU.D3, S1.Pin_3, S1.Pin_4

custom parts:
  nRF24L01: nRF24L01 module
