# Fritzing sketch promini (saved by Fritzing 0.9.2b)
breadboards: 1

parts:
  MCU = Arduino Pro Mini v13
  C1 = Electrolytic Capacitor [capacitance=1µF package="100 mil [THT, electrolytic]"]
  R1 = Resistor [tolerance=±5% resistance=220 package=THT]
  R2 = Resistor [tolerance=±5% resistance=100 package=THT]
  S1 = Pushbutton [package="[THT]"]
  nRF24L1 = nRF24L01

nets:
  GND: MCU.GND, C1.-, R1.Pin_0, S1.Pin_1, S1.Pin_2, nRF24L1.GND
  N1: MCU.VCC, R2.Pin_1
  N2: MCU.D13/SCK, nRF24L1.SCK
  N3: MCU.D12/MISO, nRF24L1.MISO
  N4: MCU.D11_PWM/MOSI, nRF24L1.MOSI
  N5: MCU.D10_PWM/SS, nRF24L1.CSN
  N6: MCU.D9_PWM, nRF24L1.CE
  N7: MCU.D3_PWM, S1.Pin_3, S1.Pin_4
  N8: C1.+, R1.Pin_1, R2.Pin_0, nRF24L1.VCC

custom parts:
  nRF24L01: nRF24L01 module
